# Fritzing sketch 555timer (saved by Fritzing 0.9.2b)
breadboards: 1

parts:
  U1 = 555 Timer [package="DIP8 [THT]"]
  Part1 = Arduino Uno (Rev3)
  R1 = Resistor [tolerance=±5% resistance=10k package=THT]
  R2 = Resistor [tolerance=±5% resistance=10k package=THT]
  C1 = Electrolytic Capacitor [capacitance=1µF package="100 mil [THT, electrolytic]"]
  C2 = Ceramic Capacitor [capacitance=100nF package="100 mil [THT, multilayer]"]
  Q1 = NPN-Transistor [package="TO92 [THT]"]
  R3 = Resistor [tolerance=±5% resistance=220 package=THT]
  LED1 = LED - 5mm [color="Red (633nm)" package="5 mm [THT]"]

nets:
  N1: U1.Ground, U1.Vcc_Supply_Voltage, Part1.GND, R1.Pin_1, C1.-, C2.1, Q1.C
  N2: U1.Trigger, U1.Threshold, R2.Pin_0, C1.+
  N3: U1.Output, Q1.B
  N4: U1.Reset, Part1.5V, LED1.cathode
  N5: U1.Control_Voltage, C2.0
  N6: U1.Discharge, R1.Pin_0, R2.Pin_1
  N7: Q1.E, R3.Pin_1
  N8: R3.Pin_0, LED1.anode
