# Fritzing sketch DHT + RGB LED (saved by Fritzing 0.9.0b)
breadboards: 1

parts:
  Part1 = Arduino Uno (Rev3)
  LED1 = RGB LED - (4 legs) [package="5 mm [THT]"]
  R1 = Resistor [tolerance=±5% resistance=220 package=THT]
  R2 = Resistor [tolerance=±5% resistance=220 package=THT]
  R3 = Resistor [tolerance=±5% resistance=220 package=THT]
  R4 = Resistor [tolerance=±5% resistance=100 package=THT]

nets:
  N1: Part1.D11_PWM/MOSI, R3.Pin_1
  N2: Part1.D12/MISO, R2.Pin_1
  N3: Part1.D13/SCK, R1.Pin_0
  N4: Part1.D5_PWM, R4.Pin_0
  N5: Part1.5V, LED1.common_anode, R4.Pin_1
  N6: LED1.red_cathode, R1.Pin_1
  N7: LED1.green_cathode, R2.Pin_0
  N8: LED1.blue_cathode, R3.Pin_0
