# Fritzing sketch Single DC engine (saved by Fritzing 0.9.0b)
breadboards: 1

parts:
  Part1 = Arduino Uno (Rev3)
  VCC1 = Battery
  U1 = TRANSISTOR_NPN_2 [package=to-92]
  M1 = DC Motor

nets:
  N1: Part1.D4, U1.B
  N2: Part1.GND, VCC1.-, U1.E
  N3: VCC1.+, M1.pin_1
  N4: U1.C, M1.pin_2
