# Fritzing sketch grajka (saved by Fritzing 0.9.0b)
breadboards: 1

parts:
  J1 = Piezo Speaker
  Part1 = Arduino Uno (Rev3)
  R1 = Rotary Potentiometer (Small) [maximum_resistance=100kΩ package=THT]

nets:
  N1: J1.pin1, Part1.GND, R1.leg1
  N2: J1.pin2, R1.wiper
  N3: Part1.D9_PWM, R1.leg2
