# Fritzing sketch przekaznik (saved by Fritzing 0.9.0b)
breadboards: 1

parts:
  Part1 = Arduino Uno (Rev3)
  LED1 = smd LED [color="Red (633nm)" package="0603 [SMD]"]
  R1 = Resistor [package="2512 [SMD]"]

nets:
  N1: Part1.GND, LED1.cathode
  N2: LED1.anode, R1.Pin_0

notes:
  Przekaźnik
  VCC NC
  GND NC
  IN NO
  COM }
  GND }
