# Fritzing sketch RezystorSzeregowo (saved by Fritzing 0.9.2b)
breadboards: 1

parts:
  Part1 = Arduino Uno (Rev3)
  R1 = Resistor [tolerance=±5% resistance=5.1k package=THT]
  R2 = Resistor [tolerance=±5% resistance=5.1k package=THT]
  R3 = Resistor [tolerance=±5% resistance=220 package=THT]
  LED1 = LED - 5mm [color="Red (633nm)" package="5 mm [THT]"]

nets:
  N1: Part1.D13/SCK, R1.Pin_0
  N2: Part1.GND, LED1.anode
  N3: R1.Pin_1, R2.Pin_0
  N4: R2.Pin_1, R3.Pin_0
  N5: R3.Pin_1, LED1.cathode
